# Fritzing sketch Heartpattern (saved by Fritzing 0.9.3b)
breadboards: 1

parts:
  LED1 = LED - 5mm [color="Red (633nm)" package="5 mm [THT]"]
  LED2 = LED - 5mm [color="Red (633nm)" package="5 mm [THT]"]
  LED3 = LED - 5mm [color="Red (633nm)" package="5 mm [THT]"]
  LED4 = LED - 5mm [color="Red (633nm)" package="5 mm [THT]"]
  LED5 = LED - 5mm [color="Red (633nm)" package="5 mm [THT]"]
  LED6 = LED - 5mm [color="Red (633nm)" package="5 mm [THT]"]
  LED7 = LED - 5mm [color="Red (633nm)" package="5 mm [THT]"]
  LED8 = LED - 5mm [color="Red (633nm)" package="5 mm [THT]"]
  LED9 = LED - 5mm [color="Red (633nm)" package="5 mm [THT]"]
  LED10 = LED - 5mm [color="Red (633nm)" package="5 mm [THT]"]
  R1 = Resistor [tolerance=±5% resistance=220 package="0402 [SMD]"]
  R2 = Resistor [tolerance=±5% resistance=220 package="0402 [SMD]"]
  R3 = Resistor [tolerance=±5% resistance=220 package="0402 [SMD]"]  # not connected
  R4 = Resistor [tolerance=±5% resistance=220 package="0402 [SMD]"]
  R5 = Resistor [tolerance=±5% resistance=220 package="0603 [SMD]"]
  R6 = Resistor [tolerance=±5% resistance=220 package="0603 [SMD]"]
  R7 = Resistor [tolerance=±5% resistance=220 package="0603 [SMD]"]
  R8 = Resistor [tolerance=±5% resistance=220 package="0603 [SMD]"]
  R9 = Resistor [tolerance=±5% resistance=220 package="0603 [SMD]"]
  Composant1 = Arduino Uno (Rev3)
  R10 = Resistor [tolerance=±5% resistance=220 package="2512 [SMD]"]

nets:
  N1: LED1.cathode, R2.Pin_1
  N2: LED1.anode, LED2.anode, LED3.anode, LED5.anode, LED6.cathode, LED7.cathode, LED9.anode, LED10.anode, R4.Pin_1, R5.Pin_0
  N3: LED2.cathode, R1.Pin_1
  N4: LED3.cathode, R6.Pin_0
  N5: LED4.cathode, Composant1.D8
  N6: LED4.anode, R1.Pin_0
  N7: LED7.anode, R7.Pin_0
  N8: LED8.anode, R8.Pin_0
  N9: LED9.cathode, R9.Pin_1
  N10: LED10.cathode, R10.Pin_1
  N11: R4.Pin_0, Composant1.D4
  N12: R8.Pin_1, Composant1.D11_PWM/MOSI
  N13: R9.Pin_0, Composant1.D6_PWM
  N14: Composant1.D5_PWM, R10.Pin_0
